// Logisim project 8_bit_router.circ as structural Verilog: 7 circuits, main circuit compare(8)
module router (
  input  [7:0] address,
  input  [1:0] p,
  input  setup,
  input  CLK,
  output [1:0] port
);

  wire or_1_out, or_2_out, or_3_out, or_4_out, or_5_out, or_6_out, or_7_out;
  wire [1:0] multiplexer_1_out, ports_1_port_2;
  wire [2:0] encoder_3_1_encoder;
  wire [7:0] addresses_1_index;

  addresses addresses_1 (.setup(setup), .Address(address), .index(addresses_1_index), .CLK(CLK));
  // Probe on address
  or or_1 (or_1_out, addresses_1_index[0], addresses_1_index[1]);
  or or_2 (or_2_out, addresses_1_index[2], addresses_1_index[3]);
  or or_3 (or_3_out, addresses_1_index[4], addresses_1_index[5]);
  or or_4 (or_4_out, addresses_1_index[6], addresses_1_index[7]);
  or or_5 (or_5_out, or_1_out, or_2_out);
  or or_6 (or_6_out, or_3_out, or_4_out);
  encoder_3 encoder_3_1 (.D_0(addresses_1_index), .encoder(encoder_3_1_encoder));
  or or_7 (or_7_out, or_5_out, or_6_out);
  ports ports_1 (.setup(setup), .Port(p), .CLK(CLK), .index(encoder_3_1_encoder), .port_2(ports_1_port_2));
  Register #(.width(2)) register_1 (.D(multiplexer_1_out), .Q(port), .clk(CLK));  // open: en, clr
  Multiplexer #(.width(2), .enable("false")) multiplexer_1 (
    .in0(2'b00), .in1(ports_1_port_2), .out(multiplexer_1_out), .sel(or_7_out));
endmodule

module compare_8 (
  input  [7:0] table_address,
  input  [7:0] \input ,
  output equality
);

  wire or_1_out, or_2_out, or_3_out, or_4_out, or_5_out, or_6_out, or_7_out, xor_1_out, xor_2_out, xor_3_out,
       xor_4_out, xor_5_out, xor_6_out, xor_7_out, xor_8_out;

  xor xor_1 (xor_1_out, table_address[0], \input [0]);
  xor xor_2 (xor_2_out, table_address[1], \input [1]);
  xor xor_3 (xor_3_out, table_address[2], \input [2]);
  xor xor_4 (xor_4_out, table_address[3], \input [3]);
  xor xor_5 (xor_5_out, table_address[4], \input [4]);
  xor xor_6 (xor_6_out, table_address[5], \input [5]);
  xor xor_7 (xor_7_out, table_address[6], \input [6]);
  xor xor_8 (xor_8_out, table_address[7], \input [7]);
  or or_1 (or_1_out, xor_1_out, xor_2_out);
  or or_2 (or_2_out, xor_3_out, xor_4_out);
  or or_3 (or_3_out, xor_5_out, xor_6_out);
  or or_4 (or_4_out, xor_7_out, xor_8_out);
  or or_5 (or_5_out, or_1_out, or_2_out);
  or or_6 (or_6_out, or_3_out, or_4_out);
  or or_7 (or_7_out, or_5_out, or_6_out);
  not not_1 (equality, or_7_out);
endmodule

module addresses (
  input  setup,
  input  CLK,
  input  [7:0] Address,
  output [7:0] index
);

  wire [7:0] multiplexer_1_out, multiplexer_2_out, multiplexer_3_out, multiplexer_4_out, multiplexer_5_out,
       multiplexer_6_out, multiplexer_7_out, multiplexer_8_out, register_1_q, register_2_q, register_3_q,
       register_4_q, register_5_q, register_6_q, register_7_q, register_8_q, register_9_q, register_10_q,
       register_11_q, register_12_q, register_13_q, register_14_q, register_15_q, register_16_q;

  Register register_1 (.D(multiplexer_1_out), .Q(register_1_q), .clk(CLK));  // open: en, clr
  Multiplexer #(.width(8), .enable("false")) multiplexer_1 (
    .in0(register_2_q), .in1(Address), .out(multiplexer_1_out), .sel(setup));
  Register register_2 (.D(multiplexer_1_out), .Q(register_2_q), .clk(CLK));  // open: en, clr
  Multiplexer #(.width(8), .enable("false")) multiplexer_2 (
    .in0(register_3_q), .in1(register_1_q), .out(multiplexer_2_out), .sel(setup));
  Register register_3 (.D(multiplexer_2_out), .Q(register_3_q), .clk(CLK));  // open: en, clr
  compare_8 compare_8_1 (.table_address(register_1_q), .\input (Address), .equality(index[7]));
  Register register_4 (.D(multiplexer_2_out), .Q(register_4_q), .clk(CLK));  // open: en, clr
  compare_8 compare_8_2 (.table_address(register_4_q), .\input (Address), .equality(index[6]));
  Multiplexer #(.width(8), .enable("false")) multiplexer_3 (
    .in0(register_5_q), .in1(register_4_q), .out(multiplexer_3_out), .sel(setup));
  Register register_5 (.D(multiplexer_3_out), .Q(register_5_q), .clk(CLK));  // open: en, clr
  Register register_6 (.D(multiplexer_3_out), .Q(register_6_q), .clk(CLK));  // open: en, clr
  Register register_7 (.D(multiplexer_4_out), .Q(register_7_q), .clk(CLK));  // open: en, clr
  compare_8 compare_8_3 (.table_address(register_6_q), .\input (Address), .equality(index[5]));
  Register register_8 (.D(multiplexer_4_out), .Q(register_8_q), .clk(CLK));  // open: en, clr
  Multiplexer #(.width(8), .enable("false")) multiplexer_4 (
    .in0(register_7_q), .in1(register_6_q), .out(multiplexer_4_out), .sel(setup));
  Multiplexer #(.width(8), .enable("false")) multiplexer_5 (
    .in0(register_9_q), .in1(register_8_q), .out(multiplexer_5_out), .sel(setup));
  Register register_9 (.D(multiplexer_5_out), .Q(register_9_q), .clk(CLK));  // open: en, clr
  compare_8 compare_8_4 (.table_address(register_8_q), .\input (Address), .equality(index[4]));
  Register register_10 (.D(multiplexer_5_out), .Q(register_10_q), .clk(CLK));  // open: en, clr
  Register register_11 (.D(multiplexer_6_out), .Q(register_11_q), .clk(CLK));  // open: en, clr
  compare_8 compare_8_5 (.table_address(register_10_q), .\input (Address), .equality(index[3]));
  Register register_12 (.D(multiplexer_6_out), .Q(register_12_q), .clk(CLK));  // open: en, clr
  Multiplexer #(.width(8), .enable("false")) multiplexer_6 (
    .in0(register_11_q), .in1(register_10_q), .out(multiplexer_6_out), .sel(setup));
  Multiplexer #(.width(8), .enable("false")) multiplexer_7 (
    .in0(register_13_q), .in1(register_12_q), .out(multiplexer_7_out), .sel(setup));
  Register register_13 (.D(multiplexer_7_out), .Q(register_13_q), .clk(CLK));  // open: en, clr
  compare_8 compare_8_6 (.table_address(register_12_q), .\input (Address), .equality(index[2]));
  Register register_14 (.D(multiplexer_7_out), .Q(register_14_q), .clk(CLK));  // open: en, clr
  compare_8 compare_8_7 (.table_address(register_14_q), .\input (Address), .equality(index[1]));
  Multiplexer #(.width(8), .enable("false")) multiplexer_8 (
    .in0(register_15_q), .in1(register_14_q), .out(multiplexer_8_out), .sel(setup));
  Register register_15 (.D(multiplexer_8_out), .Q(register_15_q), .clk(CLK));  // open: en, clr
  Register register_16 (.D(multiplexer_8_out), .Q(register_16_q), .clk(CLK));  // open: en, clr
  compare_8 compare_8_8 (.table_address(register_16_q), .\input (Address), .equality(index[0]));

  // Other names for the same wires on the sheet: CLOCK = CLK
endmodule

module ports (
  input  setup,
  input  [2:0] index,
  input  CLK,
  input  [1:0] Port,
  output [1:0] port_2
);

  wire [1:0] multiplexer_1_out, multiplexer_2_out, multiplexer_3_out, multiplexer_5_out, multiplexer_6_out,
       multiplexer_7_out, multiplexer_8_out, multiplexer_9_out, register_1_q, register_2_q, register_3_q,
       register_4_q, register_5_q, register_6_q, register_7_q, register_8_q, register_9_q, register_10_q,
       register_11_q, register_12_q, register_13_q, register_14_q, register_15_q, register_16_q;

  Register #(.width(2)) register_1 (.D(multiplexer_1_out), .Q(register_1_q), .clk(CLK));  // open: en, clr
  Multiplexer #(.width(2), .enable("false")) multiplexer_1 (
    .in0(register_2_q), .in1(Port), .out(multiplexer_1_out), .sel(setup));
  Register #(.width(2)) register_2 (.D(multiplexer_1_out), .Q(register_2_q), .clk(CLK));  // open: en, clr
  Multiplexer #(.width(2), .enable("false")) multiplexer_2 (
    .in0(register_3_q), .in1(register_1_q), .out(multiplexer_2_out), .sel(setup));
  Register #(.width(2)) register_3 (.D(multiplexer_2_out), .Q(register_3_q), .clk(CLK));  // open: en, clr
  Register #(.width(2)) register_4 (.D(multiplexer_2_out), .Q(register_4_q), .clk(CLK));  // open: en, clr
  Multiplexer #(.width(2), .enable("false")) multiplexer_3 (
    .in0(register_5_q), .in1(register_4_q), .out(multiplexer_3_out), .sel(setup));
  Register #(.width(2)) register_5 (.D(multiplexer_3_out), .Q(register_5_q), .clk(CLK));  // open: en, clr
  Register #(.width(2)) register_6 (.D(multiplexer_3_out), .Q(register_6_q), .clk(CLK));  // open: en, clr
  Register #(.width(2)) register_7 (.D(multiplexer_5_out), .Q(register_7_q), .clk(CLK));  // open: en, clr
  Multiplexer #(.select(3), .width(2), .enable("false")) multiplexer_4 (
    .in0(register_16_q), .in1(register_14_q), .in2(register_12_q), .in3(register_10_q), .in4(register_8_q),
    .in5(register_6_q), .in6(register_4_q), .in7(register_1_q), .out(port_2), .sel(index));
  Register #(.width(2)) register_8 (.D(multiplexer_5_out), .Q(register_8_q), .clk(CLK));  // open: en, clr
  Multiplexer #(.width(2), .enable("false")) multiplexer_5 (
    .in0(register_7_q), .in1(register_6_q), .out(multiplexer_5_out), .sel(setup));
  Multiplexer #(.width(2), .enable("false")) multiplexer_6 (
    .in0(register_9_q), .in1(register_8_q), .out(multiplexer_6_out), .sel(setup));
  Register #(.width(2)) register_9 (.D(multiplexer_6_out), .Q(register_9_q), .clk(CLK));  // open: en, clr
  Register #(.width(2)) register_10 (.D(multiplexer_6_out), .Q(register_10_q), .clk(CLK));  // open: en, clr
  Register #(.width(2)) register_11 (.D(multiplexer_7_out), .Q(register_11_q), .clk(CLK));  // open: en, clr
  Register #(.width(2)) register_12 (.D(multiplexer_7_out), .Q(register_12_q), .clk(CLK));  // open: en, clr
  Multiplexer #(.width(2), .enable("false")) multiplexer_7 (
    .in0(register_11_q), .in1(register_10_q), .out(multiplexer_7_out), .sel(setup));
  Multiplexer #(.width(2), .enable("false")) multiplexer_8 (
    .in0(register_13_q), .in1(register_12_q), .out(multiplexer_8_out), .sel(setup));
  Register #(.width(2)) register_13 (.D(multiplexer_8_out), .Q(register_13_q), .clk(CLK));  // open: en, clr
  Register #(.width(2)) register_14 (.D(multiplexer_8_out), .Q(register_14_q), .clk(CLK));  // open: en, clr
  Multiplexer #(.width(2), .enable("false")) multiplexer_9 (
    .in0(register_15_q), .in1(register_14_q), .out(multiplexer_9_out), .sel(setup));
  Register #(.width(2)) register_15 (.D(multiplexer_9_out), .Q(register_15_q), .clk(CLK));  // open: en, clr
  Register #(.width(2)) register_16 (.D(multiplexer_9_out), .Q(register_16_q), .clk(CLK));  // open: en, clr

  // Other names for the same wires on the sheet: CLOCK = CLK
endmodule

module encoder_3 (
  input  [7:0] D_0,
  output [2:0] encoder
);

  wire or_5_out, or_6_out;
  wire [3:0] or_1_out;

  or or_1 (or_1_out[0], D_0[0], D_0[4]);
  or or_2 (or_1_out[1], D_0[1], D_0[5]);
  or or_3 (or_1_out[2], D_0[2], D_0[6]);
  or or_4 (or_1_out[3], D_0[3], D_0[7]);
  or or_5 (or_5_out, D_0[4], D_0[5]);
  or or_6 (or_6_out, D_0[6], D_0[7]);
  encoder_2 encoder_2_1 (.D_0(or_1_out), .encoded(encoder[1:0]));
  or or_7 (encoder[2], or_5_out, or_6_out);
endmodule

module encoder_2 (
  input  [3:0] D_0,
  output [1:0] encoded
);

  wire or_1_out, or_2_out;

  or or_1 (or_1_out, D_0[0], D_0[2]);
  or or_2 (or_2_out, D_0[1], D_0[3]);
  or or_3 (encoded[1], D_0[2], D_0[3]);
  encoder_1 encoder_1_1 (.X_0(or_1_out), .X_1(or_2_out), .Y(encoded[0]));
endmodule

module encoder_1 (
  input  X_0,
  input  X_1,
  output Y
);


  assign Y = X_1;
endmodule
